# Fritzing sketch dfu_update (saved by Fritzing 1.0.4)
breadboards: 2

parts:
  Micro_uSB = Adafruit Micro USB Breakout [part_number="Adafruit #1833"]
  DFU_Mode = SWITCH_SPDT [package=kps-1290]
  RN-52 = RN-52 Breakout
  CMD_MODE = SWITCH_SPDT [package=kps-1290]
  FTDI = SparkFun FTDI Basic Breakout - 3.3V [part_number=DEV-09873]
  Power_Supply = Breadboard Power Supply Board SMD

nets (from the schematic view):
  GND: Micro_uSB.GND, RN-52.GND, CMD_MODE.P, FTDI.GND, Power_Supply.GND
  N1: Micro_uSB.D+, RN-52.USBD+
  N2: Micro_uSB.D-, RN-52.USBD-
  N3: DFU_Mode.O, RN-52.GPIO3
  3.3 V: DFU_Mode.P, RN-52.3.3V, RN-52.PWREN, Power_Supply.VCC
  N4: RN-52.UART_RX, FTDI.TXO
  N5: RN-52.UART_TX, FTDI.RXI
  N6: RN-52.GPIO9, CMD_MODE.O

custom parts:
  Adafruit Micro USB Breakout: Simple but effective - this breakout board has a USB Micro-B connector, with all 5 pins broken out. Great for pairing with a microcontroller with USB support, or adding USB 5V power to a project. We use a micro-AB connector with through-hole shielding pads for an excellent strong connection - it won't rip off by accident! Comes with one fully assembled and tested micro B breakout PCB and a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
  RN-52 Breakout: RN-52 Breakout with smaller schematic footprint
  SparkFun FTDI Basic Breakout - 3.3V: Description: This is the newest revision of our FTDI Basic. We now use a SMD 6-pin header on the bottom, which makes it smaller and more compact. Functionality has remained the same. This is a basic breakout board for the FTDI FT232RL USB to serial IC. The pinout of this board matches the FTDI cable to work with official Arduino and cloned 3.3V Arduino boards. It can also be used for general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
